# Fritzing sketch Robot_schematic_final (saved by Fritzing 0.9.3b)
breadboards: 1

parts:
  Part1 = Arduino Uno (Rev3)
  IC1 = L293D [package=THT]
  M1 = DC Motor
  M2 = DC Motor
  hc-sr1 = hc-sr04
  BAT1 = BC9VPC [package=bc9vpc]
  U1 = 74HC00 [part_number=SN74HC00N package="DIP14 [THT]"]

nets:
  N1: Part1.D11_PWM/MOSI, hc-sr1.Echo
  5V: Part1.D12/MISO, Part1.5V, IC1.+V, hc-sr1.Trig, U1.1B, U1.4A, U1.VCC
  GND: Part1.GND, IC1.0V, hc-sr1.GND, BAT1.V-, U1.GND
  N2: Part1.D4, IC1.In_1, U1.1A
  N3: Part1.D5_PWM, IC1.Enable_1
  N4: Part1.D6_PWM, IC1.Enable_2
  N5: Part1.D7, IC1.In_4, U1.4B
  N6: IC1.Out_1_(_Controlled_by_Enable_1_), M2.pin_1
  N7: IC1.Out_2_(_Controlled_by_Enable_1_), M2.pin_2
  N8: IC1.In_2, U1.1Y
  N9: IC1.+Vmotor, BAT1.V+
  N10: IC1.In_3, U1.4Y
  N11: IC1.Out_3_(_Controlled_by_Enable_2_), M1.pin_2
  N12: IC1.Out_4_(_Controlled_by_Enable_2_), M1.pin_1

custom parts:
  74HC00: Quad 2 input NAND logic gates.
