# Fritzing sketch Untitled Sketch (saved by Fritzing 0.9.3b)
breadboards: 1

parts:
  Part1 = Arduino Uno (Rev3)
  IC1 = L293D [package=THT]
  M1 = DC Motor
  M2 = DC Motor
  hc-sr1 = hc-sr04
  BAT1 = BC9VPC [package=bc9vpc]

nets:
  N1: Part1.D11_PWM/MOSI, hc-sr1.Echo
  N2: Part1.D12/MISO, Part1.5V, IC1.+V, hc-sr1.Trig
  N3: Part1.D4, IC1.In_1
  N4: Part1.D5_PWM, IC1.Enable_1
  N5: Part1.D6_PWM, IC1.Enable_2
  N6: Part1.D7, IC1.In_4
  GND: Part1.GND, IC1.0V, hc-sr1.GND, BAT1.V-
  N7: IC1.Out_1_(_Controlled_by_Enable_1_), M2.pin_1
  N8: IC1.Out_2_(_Controlled_by_Enable_1_), M2.pin_2
  N9: IC1.+Vmotor, BAT1.V+
  N10: IC1.Out_3_(_Controlled_by_Enable_2_), M1.pin_2
  N11: IC1.Out_4_(_Controlled_by_Enable_2_), M1.pin_1
